# Fritzing sketch BeeModem R1 (saved by Fritzing 0.9.3b)
circuit board: 5.68125cm x 5.56192cm
breadboards: 1

parts:
  SuperBee = XBee
  1 = Pad [width=3.03585894193728 height=6.87308646450179 connect=center]
  Reset = Pushbutton [package="[THT]"]
  1_2 = single row smd female pin header, 1 pin [form="♀ (female)"]
  2 = single row smd female pin header, 1 pin [form="♀ (female)"]
  3 = single row smd female pin header, 1 pin [form="♀ (female)"]
  12 = single row smd female pin header, 1 pin [form="♀ (female)"]
  U1 = PNP-Transistor [part_number=MCP1700 package="TO92 [THT]"]
  3_2 = Pad [width=3.03585894193728 height=6.87308646450179 connect=center]
  4 = Pad [width=3.03585894193728 height=6.87308646450179 connect=center]  # not connected
  2_2 = Pad [width=3.03585894193728 height=6.87308646450179 connect=center]
  5 = Pad [width=3.03585894193728 height=6.87308646450179 connect=center]  # not connected
  6 = Pad [width=3.03585894193728 height=6.87308646450179 connect=center]
  7 = Pad [width=3.03585894193728 height=6.87308646450179 connect=center]  # not connected
  8 = Pad [width=3.03585894193728 height=6.87308646450179 connect=center]  # not connected
  9 = Pad [width=3.03585894193728 height=6.87308646450179 connect=center]  # not connected
  10 = Pad [width=3.03585894193728 height=6.87308646450179 connect=center]  # not connected
  11 = Pad [width=3.03585894193728 height=6.87308646450179 connect=center]  # not connected
  12_2 = Pad [width=3.03585894193728 height=6.87308646450179 connect=center]
  VIN = 2.1mm DC Barrel Jack
  N = Pad [width=3.03585894193728 height=6.87308646450179 connect=center]
  B = Pad [width=3.03585894193728 height=6.87308646450179 connect=center]
  C = Pad [width=3.03585894193728 height=6.87308646450179 connect=center]
  D = Pad [width=3.03585894193728 height=6.87308646450179 connect=center]
  E = Pad [width=3.03585894193728 height=6.87308646450179 connect=center]
  F = Pad [width=3.03585894193728 height=6.87308646450179 connect=center]
  H = Pad [width=3.03585894193728 height=6.87308646450179 connect=center]
  J = Pad [width=3.03585894193728 height=6.87308646450179 connect=center]
  K = Pad [width=3.03585894193728 height=6.87308646450179 connect=center]
  L = Pad [width=3.03585894193728 height=6.87308646450179 connect=center]
  M = Pad [width=3.03585894193728 height=6.87308646450179 connect=center]
  D_2 = single row smd female pin header, 1 pin [form="♀ (female)"]
  M_2 = single row smd female pin header, 1 pin [form="♀ (female)"]
  A = single row smd female pin header, 1 pin [form="♀ (female)"]
  H_2 = single row smd female pin header, 1 pin [form="♀ (female)"]
  F_2 = single row smd female pin header, 1 pin [form="♀ (female)"]
  C_2 = single row smd female pin header, 1 pin [form="♀ (female)"]
  Reset_2 = Pushbutton [package="[THT]"]
  E_2 = single row smd female pin header, 1 pin [form="♀ (female)"]
  L_2 = single row smd female pin header, 1 pin [form="♀ (female)"]
  B_2 = single row smd female pin header, 1 pin [form="♀ (female)"]
  J_2 = single row smd female pin header, 1 pin [form="♀ (female)"]
  K_2 = single row smd female pin header, 1 pin [form="♀ (female)"]
  N_2 = single row smd female pin header, 1 pin [form="♀ (female)"]
  A_2 = Pad [width=3.03585894193728 height=6.87308646450179 connect=center]  # not connected
  Pad1 = Pad [width=5.22210362219904 height=1.7 connect=center]  # not connected
  UP9600 = male pin header, 2 pins [form="♂ (male)"]
  5_2 = single row smd female pin header, 1 pin [form="♀ (female)"]
  6_2 = single row smd female pin header, 1 pin [form="♀ (female)"]
  7_2 = single row smd female pin header, 1 pin [form="♀ (female)"]
  UP5V = male pin header, 2 pins [form="♂ (male)"]
  C1 = Capacitor [package=cap-pth-small-kit]
  UP9600-5 = male pin header, 2 pins [form="♂ (male)"]
  I2C = female pin header, 4 pins [form="♀ (female)"]
  I/O = female pin header, 6 pins [form="♀ (female)"]
  74LS245 = IC, DIP package, 20 pins [chip_label="74LS245 "]
  RESET = male pin header, 2 pins [form="♂ (male)"]  # not connected

nets:
  3.3V: SuperBee.VCC, U1.C, C1.1, I2C.pin3, I/O.pin2, 74LS245.pin20
  RxD_3V3: SuperBee.pin2, 74LS245.pin3
  TxD_3V3: SuperBee.pin3, 74LS245.pin18
  N1: SuperBee.pin5, Reset.Pin_1
  GND: SuperBee.GND, 1.pad, Reset.Pin_3, Reset.Pin_4, 1_2.pin1, 12.pin1, U1.E, 12_2.pad, VIN.switch, VIN.sleeve, N.pad, A.pin1, Reset_2.Pin_3, Reset_2.Pin_4, N_2.pin1, C1.2, I2C.pin4, 74LS245.pin10
  N2: 2.pin1, 2_2.pad, UP5V.pin2
  N3: 3.pin1, 3_2.pad, Reset_2.Pin_1, Reset_2.Pin_2
  5V: U1.B, VIN.center, UP5V.pin1, I/O.pin1
  N4: 6.pad, UP9600.pin1, 6_2.pin1
  RxD_5V: B.pad, C.pad, C_2.pin1, B_2.pin1, 7_2.pin1, 74LS245.pin17
  RTS_5V: D.pad, D_2.pin1
  DTR_5V: E.pad, E_2.pin1
  RI_5V: F.pad, F_2.pin1
  DCD_5V: H.pad, H_2.pin1
  N5: J.pad, J_2.pin1
  CTS_5V: K.pad, K_2.pin1
  DSR_5V: L.pad, L_2.pin1, UP9600.pin2
  TxD_5V: M.pad, M_2.pin1, UP9600-5.pin1, 74LS245.pin2
  N6: 5_2.pin1, UP9600-5.pin2
  SDA: I2C.pin1
  SCL: I2C.pin2

notes:
  RESET
  A5 SCL
  A4 SDA
  A3
  A2
  A1
  A0
  GND
  D0 RxD
  D2
  D3
  D5
  D6
  +5V
  VIN
  1
  16
  C64  BeeModem - Leif Bloomquist 2019 2v0
  Signals to C64 User Port
  TX
  RX
  Actual C64 User Port
  Wi-Fi
  Note pinout swapped!
  See MCP-1700 Datasheet
  C64
  D1 TxD
  Other Side Up!
  Serial#
  www.jammingsignal.com
  Jumper to disconnect 5V from User Port
  DIR:  A => B

custom parts:
  2.1mm DC Barrel Jack: 2.1mm DC Barrel Jack with Thru-Hole Connectors (breadboardable)
