# Fritzing sketch BeeModem R31 (saved by Fritzing 0.9.3b)
circuit board: 5.65015cm x 5.55415cm
breadboards: 1

parts:
  SuperB = XBee
  1 = Pad [width=3.03585894193728 height=6.87308646450179 connect=center]
  Reset = Pushbutton [package="[THT]"]
  1_2 = single row smd female pin header, 1 pin [form="♀ (female)"]
  2 = single row smd female pin header, 1 pin [form="♀ (female)"]
  3 = single row smd female pin header, 1 pin [form="♀ (female)"]
  12 = single row smd female pin header, 1 pin [form="♀ (female)"]
  U1 = PNP-Transistor [part_number=MCP1700 package="TO92 [THT]"]
  3_2 = Pad [width=3.03585894193728 height=6.87308646450179 connect=center]  # not connected
  4 = Pad [width=3.03585894193728 height=6.87308646450179 connect=center]  # not connected
  2_2 = Pad [width=3.03585894193728 height=6.87308646450179 connect=center]  # not connected
  5 = Pad [width=3.03585894193728 height=6.87308646450179 connect=center]  # not connected
  6 = Pad [width=3.03585894193728 height=6.87308646450179 connect=center]  # not connected
  7 = Pad [width=3.03585894193728 height=6.87308646450179 connect=center]  # not connected
  8 = Pad [width=3.03585894193728 height=6.87308646450179 connect=center]  # not connected
  9 = Pad [width=3.03585894193728 height=6.87308646450179 connect=center]  # not connected
  10 = Pad [width=3.03585894193728 height=6.87308646450179 connect=center]  # not connected
  11 = Pad [width=3.03585894193728 height=6.87308646450179 connect=center]  # not connected
  12_2 = Pad [width=3.03585894193728 height=6.87308646450179 connect=center]  # not connected
  N = Pad [width=3.03585894193728 height=6.87308646450179 connect=center]
  B = Pad [width=3.03585894193728 height=6.87308646450179 connect=center]
  C = Pad [width=3.03585894193728 height=6.87308646450179 connect=center]  # not connected
  D = Pad [width=3.03585894193728 height=6.87308646450179 connect=center]  # not connected
  E = Pad [width=3.03585894193728 height=6.87308646450179 connect=center]  # not connected
  F = Pad [width=3.03585894193728 height=6.87308646450179 connect=center]  # not connected
  H = Pad [width=3.03585894193728 height=6.87308646450179 connect=center]  # not connected
  J = Pad [width=3.03585894193728 height=6.87308646450179 connect=center]  # not connected
  K = Pad [width=3.03585894193728 height=6.87308646450179 connect=center]  # not connected
  L = Pad [width=3.03585894193728 height=6.87308646450179 connect=center]  # not connected
  M = Pad [width=3.03585894193728 height=6.87308646450179 connect=center]  # not connected
  D_2 = single row smd female pin header, 1 pin [form="♀ (female)"]
  M_2 = single row smd female pin header, 1 pin [form="♀ (female)"]
  A = single row smd female pin header, 1 pin [form="♀ (female)"]
  H_2 = single row smd female pin header, 1 pin [form="♀ (female)"]
  F_2 = single row smd female pin header, 1 pin [form="♀ (female)"]
  C_2 = single row smd female pin header, 1 pin [form="♀ (female)"]
  Reset_2 = Pushbutton [package="[THT]"]
  E_2 = single row smd female pin header, 1 pin [form="♀ (female)"]
  L_2 = single row smd female pin header, 1 pin [form="♀ (female)"]
  B_2 = single row smd female pin header, 1 pin [form="♀ (female)"]
  J_2 = single row smd female pin header, 1 pin [form="♀ (female)"]  # not connected
  K_2 = single row smd female pin header, 1 pin [form="♀ (female)"]
  N_2 = single row smd female pin header, 1 pin [form="♀ (female)"]
  A_2 = Pad [width=3.03585894193728 height=6.87308646450179 connect=center]  # not connected
  Pad1 = Pad [width=5.22210362219904 height=1.7 connect=center]  # not connected
  UP9600_+ = male pin header, 2 pins [form="♂ (male)"]
  5_2 = single row smd female pin header, 1 pin [form="♀ (female)"]
  6_2 = single row smd female pin header, 1 pin [form="♀ (female)"]
  7_2 = single row smd female pin header, 1 pin [form="♀ (female)"]
  UP5V = male pin header, 2 pins [form="♂ (male)"]
  C1 = Capacitor [package=cap-pth-small-kit]
  UP9600-5 = male pin header, 2 pins [form="♂ (male)"]
  I2C = female pin header, 4 pins [form="♀ (female)"]
  Init = male pin header, 2 pins [form="♂ (male)"]
  I/O = female pin header, 6 pins [form="♀ (female)"]
  VIN_+5V = 2.1mm DC Barrel Jack
  74LS245 = IC, DIP package, 20 pins [chip_label="74LS245 "]

nets:
  3.3V: SuperB.VCC, SuperB.pin7, U1.C, C1.1, I2C.pin3, I/O.pin1, 74LS245.pin1, 74LS245.pin20
  RxD_3V3: SuperB.pin2, 74LS245.pin3
  TxD_3V3: SuperB.pin3, 74LS245.pin18
  SDA: SuperB.pin4, I2C.pin1
  N1: SuperB.pin5, Reset.Pin_1
  SCL: SuperB.pin6, I2C.pin2
  RI_3V3: SuperB.pin8, 74LS245.pin5
  DTR_3V3: SuperB.pin9, 74LS245.pin16
  GND: SuperB.GND, 1.pad, Reset.Pin_3, Reset.Pin_4, 1_2.pin1, 12.pin1, U1.E, N.pad, A.pin1, Reset_2.Pin_3, Reset_2.Pin_4, N_2.pin1, C1.2, I2C.pin4, Init.pin2, I/O.pin6, VIN_+5V.switch, VIN_+5V.sleeve, 74LS245.pin10, 74LS245.pin19
  DCD_3V3: SuperB.pin11, 74LS245.pin7
  RTS_3V3: SuperB.pin12, 74LS245.pin14
  DSR_3V3: SuperB.pin13, 74LS245.pin9
  N2: SuperB.pin14, Init.pin1
  CTS_3V3: SuperB.pin16, 74LS245.pin8
  IO2: SuperB.pin17, I/O.pin2
  IO18: SuperB.pin18, I/O.pin3
  IO33: SuperB.pin19, I/O.pin4
  IO32: SuperB.pin20, I/O.pin5
  N3: 2.pin1, UP5V.pin2
  N4: 3.pin1, Reset_2.Pin_1, Reset_2.Pin_2
  5V: U1.B, UP5V.pin1, VIN_+5V.center
  RxD_5V: B.pad, C_2.pin1, B_2.pin1, 7_2.pin1, 74LS245.pin17
  RTS_5V: D_2.pin1, 74LS245.pin6
  TxD_5V: M_2.pin1, UP9600-5.pin1, 74LS245.pin2
  DCD_5V: H_2.pin1, 74LS245.pin13
  RI_5V: F_2.pin1, 74LS245.pin15
  DTR_5V: E_2.pin1, 74LS245.pin4
  DSR_5V: L_2.pin1, UP9600_+.pin2, 74LS245.pin11
  CTS_5V: K_2.pin1, 74LS245.pin12
  N5: UP9600_+.pin1, 6_2.pin1
  N6: 5_2.pin1, UP9600-5.pin2

notes:
  SCL
  SDA
  GND
  3.3V
  Commodore SuperB Modem   Leif Bloomquist 2019 2v002 R32
  Signals to C64 User Port
  TX
  RX
  Actual C64 User Port
  Wi-Fi
  Note pinout swapped!
  See MCP-1700 Datasheet
  C64
  Other Side Up!
  Serial#
  www.jammingsignal.com
  Jumper to disconnect 5V from User Port
  DIR:  A => B
  VIN +5V
  VCC
  _________
  IO32
  IO33
  IO18
  IO2
  Pin15=IO26=LED Don't connect

custom parts:
  2.1mm DC Barrel Jack: 2.1mm DC Barrel Jack with Thru-Hole Connectors (breadboardable)
