# Fritzing sketch BeeModem R48 TTGO (saved by Fritzing 0.9.3b)
circuit board: 5.65015cm x 5.55415cm
breadboards: 1

parts:
  1 = Pad [width=3.03585894193728 height=6.87308646450179 connect=center]  # not connected
  2 = single row smd female pin header, 1 pin [form="♀ (female)"]
  12 = single row smd female pin header, 1 pin [form="♀ (female)"]
  3 = Pad [width=3.03585894193728 height=6.87308646450179 connect=center]
  4 = Pad [width=3.03585894193728 height=6.87308646450179 connect=center]  # not connected
  2_2 = Pad [width=3.03585894193728 height=6.87308646450179 connect=center]  # not connected
  5 = Pad [width=3.03585894193728 height=6.87308646450179 connect=center]
  6 = Pad [width=3.03585894193728 height=6.87308646450179 connect=center]  # not connected
  7 = Pad [width=3.03585894193728 height=6.87308646450179 connect=center]  # not connected
  8 = Pad [width=3.03585894193728 height=6.87308646450179 connect=center]  # not connected
  9 = Pad [width=3.03585894193728 height=6.87308646450179 connect=center]  # not connected
  10 = Pad [width=3.03585894193728 height=6.87308646450179 connect=center]
  11 = Pad [width=3.03585894193728 height=6.87308646450179 connect=center]  # not connected
  12_2 = Pad [width=3.03585894193728 height=6.87308646450179 connect=center]
  N = Pad [width=3.03585894193728 height=6.87308646450179 connect=center]  # not connected
  B = Pad [width=3.03585894193728 height=6.87308646450179 connect=center]  # not connected
  C = Pad [width=3.03585894193728 height=6.87308646450179 connect=center]
  D = Pad [width=3.03585894193728 height=6.87308646450179 connect=center]  # not connected
  E = Pad [width=3.03585894193728 height=6.87308646450179 connect=center]
  F = Pad [width=3.03585894193728 height=6.87308646450179 connect=center]  # not connected
  H = Pad [width=3.03585894193728 height=6.87308646450179 connect=center]  # not connected
  J = Pad [width=3.03585894193728 height=6.87308646450179 connect=center]  # not connected
  K = Pad [width=3.03585894193728 height=6.87308646450179 connect=center]  # not connected
  L = Pad [width=3.03585894193728 height=6.87308646450179 connect=center]  # not connected
  M = Pad [width=3.03585894193728 height=6.87308646450179 connect=center]  # not connected
  D_2 = single row smd female pin header, 1 pin [form="♀ (female)"]
  M_2 = single row smd female pin header, 1 pin [form="♀ (female)"]
  A = single row smd female pin header, 1 pin [form="♀ (female)"]
  H_2 = single row smd female pin header, 1 pin [form="♀ (female)"]
  F_2 = single row smd female pin header, 1 pin [form="♀ (female)"]
  C_2 = single row smd female pin header, 1 pin [form="♀ (female)"]
  Reset = Pushbutton [package="[THT]"]
  E_2 = single row smd female pin header, 1 pin [form="♀ (female)"]
  L_2 = single row smd female pin header, 1 pin [form="♀ (female)"]
  B_2 = single row smd female pin header, 1 pin [form="♀ (female)"]
  J_2 = single row smd female pin header, 1 pin [form="♀ (female)"]  # not connected
  K_2 = single row smd female pin header, 1 pin [form="♀ (female)"]
  N_2 = single row smd female pin header, 1 pin [form="♀ (female)"]
  A_2 = Pad [width=3.03585894193728 height=6.87308646450179 connect=center]  # not connected
  Pad1 = Pad [width=5.22210362219904 height=1.7 connect=center]  # not connected
  UP9600 = male pin header, 2 pins [form="♂ (male)"]
  5_2 = single row smd female pin header, 1 pin [form="♀ (female)"]
  6_2 = single row smd female pin header, 1 pin [form="♀ (female)"]
  7_2 = single row smd female pin header, 1 pin [form="♀ (female)"]  # not connected
  UP5V = male pin header, 2 pins [form="♂ (male)"]
  UP9600-5 = male pin header, 2 pins [form="♂ (male)"]
  Init = male pin header, 2 pins [form="♂ (male)"]
  VIN_+5V = 2.1mm DC Barrel Jack
  74LS245 = IC, DIP package, 20 pins [chip_label="74LS245 "]
  C1 = Capacitor [package=cap-pth-small-kit]
  ESP32_+_OLED = IC, DIP package, 36 pins [chip_label=ESP32]
  I/O = female pin header, 10 pins [form="♀ (female)"]
  3_2 = single row smd female pin header, 1 pin [form="♀ (female)"]
  1_2 = single row smd female pin header, 1 pin [form="♀ (female)"]

nets:
  N1: 2.pin1, UP5V.pin2
  GND: 12.pin1, 12_2.pad, A.pin1, Reset.Pin_3, Reset.Pin_4, N_2.pin1, Init.pin2, VIN_+5V.switch, VIN_+5V.sleeve, 74LS245.pin10, 74LS245.pin19, C1.2, ESP32_+_OLED.pin1, ESP32_+_OLED.pin36, 1_2.pin1
  N2: 3.pad, Reset.Pin_1, Reset.Pin_2, 3_2.pin1
  N3: 5.pad, 5_2.pin1, UP9600-5.pin2
  DSR_5V: 10.pad, L_2.pin1, UP9600.pin2, 74LS245.pin11
  RxD_5V: C.pad, C_2.pin1, B_2.pin1, 74LS245.pin17
  DTR_5V: E.pad, E_2.pin1, 74LS245.pin4
  RTS_5V: D_2.pin1, 74LS245.pin6
  TxD_5V: M_2.pin1, UP9600-5.pin1, 74LS245.pin2
  DCD_5V: H_2.pin1, 74LS245.pin13
  RI_5V: F_2.pin1, 74LS245.pin15
  CTS_5V: K_2.pin1, 74LS245.pin12
  N4: UP9600.pin1, 6_2.pin1
  5V: UP5V.pin1, VIN_+5V.center, C1.1, ESP32_+_OLED.pin2, ESP32_+_OLED.pin35, I/O.pin10
  N5: Init.pin1, ESP32_+_OLED.pin9
  3.3V: 74LS245.pin1, 74LS245.pin20, ESP32_+_OLED.pin3
  RxD_3V3: 74LS245.pin3, ESP32_+_OLED.pin27
  RI_3V3: 74LS245.pin5, ESP32_+_OLED.pin25
  DCD_3V3: 74LS245.pin7, ESP32_+_OLED.pin23
  CTS_3V3: 74LS245.pin8, ESP32_+_OLED.pin22
  DSR_3V3: 74LS245.pin9, ESP32_+_OLED.pin21
  RTS_3V3: 74LS245.pin14, ESP32_+_OLED.pin14
  DTR_3V3: 74LS245.pin16, ESP32_+_OLED.pin12
  TxD_3V3: 74LS245.pin18, ESP32_+_OLED.pin10
  N6: ESP32_+_OLED.pin19, I/O.pin1
  N7: ESP32_+_OLED.pin20, I/O.pin2
  N8: ESP32_+_OLED.pin24, I/O.pin3
  N9: ESP32_+_OLED.pin26, I/O.pin4
  N10: ESP32_+_OLED.pin28, I/O.pin5
  N11: ESP32_+_OLED.pin29, I/O.pin6
  N12: ESP32_+_OLED.pin30, I/O.pin7
  N13: ESP32_+_OLED.pin33, I/O.pin8
  N14: ESP32_+_OLED.pin34, I/O.pin9

notes:
  GND
  Commodore Wi-Fi Modem   Leif Bloomquist 2020 2v003 R47
  Signals to C64 User Port
  Actual C64 User Port
  C64
  Other Side Up!
  Serial#
  www.jammingsignal.com
  Jumper to disconnect 5V from User Port
  DIR:  A => B
  VIN +5V
  15
  16
  5
  2
  3.3V
  +
  5V
  0
  22
  24

custom parts:
  2.1mm DC Barrel Jack: 2.1mm DC Barrel Jack with Thru-Hole Connectors (breadboardable)
